// Logisim project CombiUnit.circ as structural Verilog: 8 circuits, main circuit 4x1 MUX
module _4x1_MUX (
  input  s1,
  input  s0,
  input  i0,
  input  i1,
  input  i2,
  input  i3,
  output \output 
);

  wire and_1_out, and_2_out, and_3_out, and_4_out, not_1_out, not_2_out;

  not not_1 (not_1_out, s1);
  not not_2 (not_2_out, s0);
  and and_1 (and_1_out, not_2_out, not_1_out, i0);
  and and_2 (and_2_out, s0, not_1_out, i1);
  and and_3 (and_3_out, not_2_out, s1, i2);
  and and_4 (and_4_out, s0, s1, i3);
  or or_1 (\output , and_3_out, and_1_out, and_2_out, and_4_out);
endmodule

module _4bit_adder (
  input  [3:0] X,
  input  Cin,
  input  [3:0] Y,
  output [3:0] _8421,
  output out_5
);

  wire full_adder_1_p5, full_adder_2_p5, full_adder_3_p5;

  // Full_Adder full_adder_1: pin names not known; wires that end beside it: X[0], Y[0], Cin, _8421[0], full_adder_1_p5
  // Full_Adder full_adder_2: pin names not known; wires that end beside it: X[1], Y[1], full_adder_1_p5, _8421[1], full_adder_2_p5
  // Full_Adder full_adder_3: pin names not known; wires that end beside it: X[2], Y[2], full_adder_2_p5, _8421[2], full_adder_3_p5
  // Full_Adder full_adder_4: pin names not known; wires that end beside it: X[3], Y[3], full_adder_3_p5, _8421[3], out_5

  // Notes on the sheet:
  //   8421
  //   8421
endmodule

module _3_8Decoder (
  input  C2,
  input  C1,
  input  C0,
  input  Enable,
  output D0,
  output D1,
  output D2,
  output D3,
  output D4,
  output D5,
  output D6,
  output D7
);

  wire not_1_out, not_2_out, not_3_out;

  not not_1 (not_1_out, C2);
  not not_2 (not_2_out, C1);
  not not_3 (not_3_out, C0);
  and and_1 (D0, not_1_out, not_2_out, not_3_out, Enable);
  and and_2 (D1, not_1_out, not_2_out, C0, Enable);
  and and_3 (D2, not_1_out, C1, C0, Enable);
  buf and_4 (D3, Enable);  // AND_Gate
  buf and_5 (D4, Enable);  // AND_Gate
  buf and_6 (D5, Enable);  // AND_Gate
  buf and_7 (D6, Enable);  // AND_Gate
  buf and_8 (D7, Enable);  // AND_Gate
endmodule

module _1bit_LU (
  input  a,
  input  b,
  input  s1,
  input  s0,
  output out_5
);

  wire and_1_out, not_1_out, or_1_out, xor_1_out;

  and and_1 (and_1_out, a, b);
  or or_1 (or_1_out, a, b);
  xor xor_1 (xor_1_out, a, b);
  not not_1 (not_1_out, a);
  Multiplexer multiplexer_1 (.in0(or_1_out), .in1(not_1_out), .out(out_5), .sel(s1), .en(s0));
endmodule

module _4bit_LU (
  input  [3:0] A,
  input  [3:0] B,
  input  s1,
  input  s0,
  output [3:0] out
);

  _1bit_LU u_1bit_lu_1 (.a(A[0]), .b(B[0]), .s1(s1), .s0(s0), .out_5(out[0]));
  _1bit_LU u_1bit_lu_2 (.a(A[1]), .b(B[1]), .s1(s1), .s0(s0), .out_5(out[1]));
  _1bit_LU u_1bit_lu_3 (.a(A[2]), .b(B[2]), .s1(s1), .s0(s0), .out_5(out[2]));
  _1bit_LU u_1bit_lu_4 (.a(A[3]), .b(B[3]), .s1(s1), .s0(s0), .out_5(out[3]));
endmodule

module main (
);

  ArithmeticUnit arithmeticunit_1 ();  // open: A, B, selector, out_4, out_5
endmodule

module ArithmeticUnit (
  input  [7:0] A,
  input  [7:0] B,
  input  selector,
  output [7:0] out_4,
  output out_5
);

  wire [7:0] multiplexer_1_out, not_1_out;

  assign not_1_out = ~B;  // NOT_Gate not_1, 8 bits wide
  Multiplexer #(.width(8)) multiplexer_1 (
    .in0(B), .in1(not_1_out), .out(multiplexer_1_out), .sel(selector));  // open: en
  Adder adder_1 (.a(A), .b(multiplexer_1_out), .out(out_4), .cin(selector), .cout(out_5));
endmodule

module LogicUnit (
  input  [7:0] A,
  input  [7:0] B,
  input  [1:0] s1,
  output [7:0] out_4
);

  wire [7:0] and_1_out, nor_1_out, or_1_out, xor_1_out;

  assign or_1_out = A | B;  // OR_Gate or_1, 8 bits wide
  assign and_1_out = A & B;  // AND_Gate and_1, 8 bits wide
  assign xor_1_out = A ^ B;  // XOR_Gate xor_1, 8 bits wide
  assign nor_1_out = ~(B | A);  // NOR_Gate nor_1, 8 bits wide
  Multiplexer #(.select(2), .width(8)) multiplexer_1 (
    .in0(or_1_out), .in1(and_1_out), .in2(xor_1_out), .in3(nor_1_out), .out(out_4), .sel(s1));  // open: en
endmodule
