// Logisim project assignment.circ as structural Verilog: 1 circuit, main circuit main
module main (
  input  [7:0] A,
  input  [7:0] B,
  input  [2:0] sel,
  output [7:0] C
);

  wire [7:0] arithmeticunit_1_out_4, logicunit_1_out_4;

  ArithmeticUnit arithmeticunit_1 (.A(A), .B(B), .selector(sel[0]), .out_4(arithmeticunit_1_out_4));  // open: out_5
  LogicUnit logicunit_1 (.A(A), .B(B), .out_4(logicunit_1_out_4));  // open: s1
  Multiplexer #(.width(8)) multiplexer_1 (
    .in0(arithmeticunit_1_out_4), .in1(logicunit_1_out_4), .out(C), .sel(sel[2]));  // open: en
endmodule
