// Logisim project final_project.circ as structural Verilog: 6 circuits, main circuit IF(수업)
module \IF_수업  (
  input  [31:0] offset,
  input  clear,
  input  branch,
  input  Zero,
  output [31:0] out_5
);

  wire and_1_out, clock_1_out;
  wire [31:0] adder_1_out, adder_2_out, multiplexer_1_out, PC_q;

  Register #(.width(32)) PC (.D(multiplexer_1_out), .Q(PC_q), .clk(clock_1_out), .clr(clear));  // open: en
  Clock clock_1 (.out(clock_1_out));
  and and_1 (and_1_out, branch, Zero);
  Adder #(.width(32)) adder_1 (.a({offset[29:0], 2'b00}), .b(PC_q), .out(adder_1_out));  // open: cin, cout
  Adder #(.width(32)) adder_2 (.a(32'h4), .b(PC_q), .out(adder_2_out));  // open: cin, cout
  Multiplexer #(.width(32), .enable("false")) multiplexer_1 (
    .in0(adder_2_out), .in1(adder_1_out), .out(multiplexer_1_out), .sel(and_1_out));
  ROM #(.dataWidth(32)) rom_1 (.addr(PC_q[9:2]), .data(out_5));  // open: sel

  // Notes on the sheet:
  //   Instruction Fetch
  //   Instruction Memory
  //   contents of rom_1 (hex, n*v repeats v):
  //   20010004 20020003 221820 ac230004 8c240004 2042ffff 1402fffc
  //   Instrution
endmodule

module register_file (
  input  [31:0] C,
  input  clk,
  input  clear,
  input  load,
  input  [4:0] rd,
  input  [4:0] rs,
  input  [4:0] rt,
  output [31:0] A,
  output [31:0] B
);

  wire decoder_1_out0, decoder_1_out1, decoder_1_out2, decoder_1_out3, decoder_1_out4, decoder_1_out5,
       decoder_1_out6, decoder_1_out7, decoder_1_out8, decoder_1_out9, decoder_1_out10, decoder_1_out11,
       decoder_1_out12, decoder_1_out13, decoder_1_out14, decoder_1_out15, decoder_1_out16, decoder_1_out17,
       decoder_1_out18, decoder_1_out19, decoder_1_out20, decoder_1_out21, decoder_1_out22, decoder_1_out23,
       decoder_1_out24, decoder_1_out25, decoder_1_out26, decoder_1_out27, decoder_1_out28, decoder_1_out29,
       decoder_1_out30, decoder_1_out31, decoder_2_out0, decoder_2_out1, decoder_2_out2, decoder_2_out3,
       decoder_2_out4, decoder_2_out5, decoder_2_out6, decoder_2_out7, decoder_2_out8, decoder_2_out9,
       decoder_2_out10, decoder_2_out11, decoder_2_out12, decoder_2_out13, decoder_2_out14, decoder_2_out15,
       decoder_2_out16, decoder_2_out17, decoder_2_out18, decoder_2_out19, decoder_2_out20, decoder_2_out21,
       decoder_2_out22, decoder_2_out23, decoder_2_out24, decoder_2_out25, decoder_2_out26, decoder_2_out27,
       decoder_2_out28, decoder_2_out29, decoder_2_out30, decoder_2_out31, demultiplexer_1_out0,
       demultiplexer_1_out1, demultiplexer_1_out2, demultiplexer_1_out3, demultiplexer_1_out4,
       demultiplexer_1_out5, demultiplexer_1_out6, demultiplexer_1_out7, demultiplexer_1_out8,
       demultiplexer_1_out9, demultiplexer_1_out10, demultiplexer_1_out11, demultiplexer_1_out12,
       demultiplexer_1_out13, demultiplexer_1_out14, demultiplexer_1_out15, demultiplexer_1_out16,
       demultiplexer_1_out17, demultiplexer_1_out18, demultiplexer_1_out19, demultiplexer_1_out20,
       demultiplexer_1_out21, demultiplexer_1_out22, demultiplexer_1_out23, demultiplexer_1_out24,
       demultiplexer_1_out25, demultiplexer_1_out26, demultiplexer_1_out27, demultiplexer_1_out28,
       demultiplexer_1_out29, demultiplexer_1_out30, demultiplexer_1_out31;
  wire [31:0] register_1_q, register_2_q, register_3_q, register_4_q, register_5_q, register_6_q,
       register_7_q, register_8_q, register_9_q, register_10_q, register_11_q, register_12_q, register_13_q,
       register_14_q, register_15_q, register_16_q, register_17_q, register_18_q, register_19_q,
       register_20_q, register_21_q, register_22_q, register_23_q, register_24_q, register_25_q,
       register_26_q, register_27_q, register_28_q, register_29_q, register_30_q, register_31_q,
       register_32_q;

  Demultiplexer #(.select(5)) demultiplexer_1 (
    .out0(demultiplexer_1_out0), .out1(demultiplexer_1_out1), .out2(demultiplexer_1_out2),
    .out3(demultiplexer_1_out3), .out4(demultiplexer_1_out4), .out5(demultiplexer_1_out5),
    .out6(demultiplexer_1_out6), .out7(demultiplexer_1_out7), .out8(demultiplexer_1_out8),
    .out9(demultiplexer_1_out9), .out10(demultiplexer_1_out10), .out11(demultiplexer_1_out11),
    .out12(demultiplexer_1_out12), .out13(demultiplexer_1_out13), .out14(demultiplexer_1_out14),
    .out15(demultiplexer_1_out15), .out16(demultiplexer_1_out16), .out17(demultiplexer_1_out17),
    .out18(demultiplexer_1_out18), .out19(demultiplexer_1_out19), .out20(demultiplexer_1_out20),
    .out21(demultiplexer_1_out21), .out22(demultiplexer_1_out22), .out23(demultiplexer_1_out23),
    .out24(demultiplexer_1_out24), .out25(demultiplexer_1_out25), .out26(demultiplexer_1_out26),
    .out27(demultiplexer_1_out27), .out28(demultiplexer_1_out28), .out29(demultiplexer_1_out29),
    .out30(demultiplexer_1_out30), .out31(demultiplexer_1_out31), .in(load), .sel(rd));  // open: en
  Register #(.width(32)) register_1 (.D(C), .en(demultiplexer_1_out0), .Q(register_1_q), .clk(clk), .clr(clear));
  Register #(.width(32)) register_2 (.D(C), .en(demultiplexer_1_out1), .Q(register_2_q), .clk(clk), .clr(clear));
  Register #(.width(32)) register_3 (.D(C), .en(demultiplexer_1_out2), .Q(register_3_q), .clk(clk), .clr(clear));
  Register #(.width(32)) register_4 (.D(C), .en(demultiplexer_1_out3), .Q(register_4_q), .clk(clk), .clr(clear));
  Register #(.width(32)) register_5 (.D(C), .en(demultiplexer_1_out4), .Q(register_5_q), .clk(clk), .clr(clear));
  Register #(.width(32)) register_6 (.D(C), .en(demultiplexer_1_out5), .Q(register_6_q), .clk(clk), .clr(clear));
  Register #(.width(32)) register_7 (.D(C), .en(demultiplexer_1_out6), .Q(register_7_q), .clk(clk), .clr(clear));
  Register #(.width(32)) register_8 (.D(C), .en(demultiplexer_1_out7), .Q(register_8_q), .clk(clk), .clr(clear));
  Register #(.width(32)) register_9 (.D(C), .en(demultiplexer_1_out8), .Q(register_9_q), .clk(clk), .clr(clear));
  Register #(.width(32)) register_10 (.D(C), .en(demultiplexer_1_out9), .Q(register_10_q), .clk(clk), .clr(clear));
  Register #(.width(32)) register_11 (.D(C), .en(demultiplexer_1_out10), .Q(register_11_q), .clk(clk), .clr(clear));
  Register #(.width(32)) register_12 (.D(C), .en(demultiplexer_1_out11), .Q(register_12_q), .clk(clk), .clr(clear));
  Register #(.width(32)) register_13 (.D(C), .en(demultiplexer_1_out12), .Q(register_13_q), .clk(clk), .clr(clear));
  Register #(.width(32)) register_14 (.D(C), .en(demultiplexer_1_out13), .Q(register_14_q), .clk(clk), .clr(clear));
  Register #(.width(32)) register_15 (.D(C), .en(demultiplexer_1_out14), .Q(register_15_q), .clk(clk), .clr(clear));
  Register #(.width(32)) register_16 (.D(C), .en(demultiplexer_1_out15), .Q(register_16_q), .clk(clk), .clr(clear));
  Register #(.width(32)) register_17 (.D(C), .en(demultiplexer_1_out16), .Q(register_17_q), .clk(clk), .clr(clear));
  Register #(.width(32)) register_18 (.D(C), .en(demultiplexer_1_out17), .Q(register_18_q), .clk(clk), .clr(clear));
  Register #(.width(32)) register_19 (.D(C), .en(demultiplexer_1_out18), .Q(register_19_q), .clk(clk), .clr(clear));
  Register #(.width(32)) register_20 (.D(C), .en(demultiplexer_1_out19), .Q(register_20_q), .clk(clk), .clr(clear));
  Register #(.width(32)) register_21 (.D(C), .en(demultiplexer_1_out20), .Q(register_21_q), .clk(clk), .clr(clear));
  Register #(.width(32)) register_22 (.D(C), .en(demultiplexer_1_out21), .Q(register_22_q), .clk(clk), .clr(clear));
  Register #(.width(32)) register_23 (.D(C), .en(demultiplexer_1_out22), .Q(register_23_q), .clk(clk), .clr(clear));
  Register #(.width(32)) register_24 (.D(C), .en(demultiplexer_1_out23), .Q(register_24_q), .clk(clk), .clr(clear));
  Register #(.width(32)) register_25 (.D(C), .en(demultiplexer_1_out24), .Q(register_25_q), .clk(clk), .clr(clear));
  Register #(.width(32)) register_26 (.D(C), .en(demultiplexer_1_out25), .Q(register_26_q), .clk(clk), .clr(clear));
  Register #(.width(32)) register_27 (.D(C), .en(demultiplexer_1_out26), .Q(register_27_q), .clk(clk), .clr(clear));
  Register #(.width(32)) register_28 (.D(C), .en(demultiplexer_1_out27), .Q(register_28_q), .clk(clk), .clr(clear));
  Register #(.width(32)) register_29 (.D(C), .en(demultiplexer_1_out28), .Q(register_29_q), .clk(clk), .clr(clear));
  Register #(.width(32)) register_30 (.D(C), .en(demultiplexer_1_out29), .Q(register_30_q), .clk(clk), .clr(clear));
  Register #(.width(32)) register_31 (.D(C), .en(demultiplexer_1_out30), .Q(register_31_q), .clk(clk), .clr(clear));
  Register #(.width(32)) register_32 (.D(C), .en(demultiplexer_1_out31), .Q(register_32_q), .clk(clk), .clr(clear));
  Decoder #(.select(5)) decoder_1 (
    .out0(decoder_1_out0), .out1(decoder_1_out1), .out2(decoder_1_out2), .out3(decoder_1_out3),
    .out4(decoder_1_out4), .out5(decoder_1_out5), .out6(decoder_1_out6), .out7(decoder_1_out7),
    .out8(decoder_1_out8), .out9(decoder_1_out9), .out10(decoder_1_out10), .out11(decoder_1_out11),
    .out12(decoder_1_out12), .out13(decoder_1_out13), .out14(decoder_1_out14), .out15(decoder_1_out15),
    .out16(decoder_1_out16), .out17(decoder_1_out17), .out18(decoder_1_out18), .out19(decoder_1_out19),
    .out20(decoder_1_out20), .out21(decoder_1_out21), .out22(decoder_1_out22), .out23(decoder_1_out23),
    .out24(decoder_1_out24), .out25(decoder_1_out25), .out26(decoder_1_out26), .out27(decoder_1_out27),
    .out28(decoder_1_out28), .out29(decoder_1_out29), .out30(decoder_1_out30), .out31(decoder_1_out31),
    .sel(rt));  // open: en
  Decoder #(.select(5)) decoder_2 (
    .out0(decoder_2_out0), .out1(decoder_2_out1), .out2(decoder_2_out2), .out3(decoder_2_out3),
    .out4(decoder_2_out4), .out5(decoder_2_out5), .out6(decoder_2_out6), .out7(decoder_2_out7),
    .out8(decoder_2_out8), .out9(decoder_2_out9), .out10(decoder_2_out10), .out11(decoder_2_out11),
    .out12(decoder_2_out12), .out13(decoder_2_out13), .out14(decoder_2_out14), .out15(decoder_2_out15),
    .out16(decoder_2_out16), .out17(decoder_2_out17), .out18(decoder_2_out18), .out19(decoder_2_out19),
    .out20(decoder_2_out20), .out21(decoder_2_out21), .out22(decoder_2_out22), .out23(decoder_2_out23),
    .out24(decoder_2_out24), .out25(decoder_2_out25), .out26(decoder_2_out26), .out27(decoder_2_out27),
    .out28(decoder_2_out28), .out29(decoder_2_out29), .out30(decoder_2_out30), .out31(decoder_2_out31),
    .sel(rs));  // open: en
  assign B = decoder_1_out0 ? register_1_q : 32'bz;  // Controlled_Buffer controlled_buffer_1
  assign B = decoder_1_out1 ? register_2_q : 32'bz;  // Controlled_Buffer controlled_buffer_2
  assign B = decoder_1_out2 ? register_3_q : 32'bz;  // Controlled_Buffer controlled_buffer_3
  assign B = decoder_1_out3 ? register_4_q : 32'bz;  // Controlled_Buffer controlled_buffer_4
  assign B = decoder_1_out4 ? register_5_q : 32'bz;  // Controlled_Buffer controlled_buffer_5
  assign B = decoder_1_out5 ? register_6_q : 32'bz;  // Controlled_Buffer controlled_buffer_6
  assign B = decoder_1_out6 ? register_7_q : 32'bz;  // Controlled_Buffer controlled_buffer_7
  assign B = decoder_1_out7 ? register_8_q : 32'bz;  // Controlled_Buffer controlled_buffer_8
  assign B = decoder_1_out8 ? register_9_q : 32'bz;  // Controlled_Buffer controlled_buffer_9
  assign B = decoder_1_out9 ? register_10_q : 32'bz;  // Controlled_Buffer controlled_buffer_10
  assign B = decoder_1_out10 ? register_11_q : 32'bz;  // Controlled_Buffer controlled_buffer_11
  assign B = decoder_1_out11 ? register_12_q : 32'bz;  // Controlled_Buffer controlled_buffer_12
  assign B = decoder_1_out12 ? register_13_q : 32'bz;  // Controlled_Buffer controlled_buffer_13
  assign B = decoder_1_out13 ? register_14_q : 32'bz;  // Controlled_Buffer controlled_buffer_14
  assign B = decoder_1_out14 ? register_15_q : 32'bz;  // Controlled_Buffer controlled_buffer_15
  assign B = decoder_1_out15 ? register_16_q : 32'bz;  // Controlled_Buffer controlled_buffer_16
  assign B = decoder_1_out16 ? register_17_q : 32'bz;  // Controlled_Buffer controlled_buffer_17
  assign B = decoder_1_out17 ? register_18_q : 32'bz;  // Controlled_Buffer controlled_buffer_18
  assign B = decoder_1_out18 ? register_19_q : 32'bz;  // Controlled_Buffer controlled_buffer_19
  assign B = decoder_1_out19 ? register_20_q : 32'bz;  // Controlled_Buffer controlled_buffer_20
  assign B = decoder_1_out20 ? register_21_q : 32'bz;  // Controlled_Buffer controlled_buffer_21
  assign B = decoder_1_out21 ? register_22_q : 32'bz;  // Controlled_Buffer controlled_buffer_22
  assign B = decoder_1_out22 ? register_23_q : 32'bz;  // Controlled_Buffer controlled_buffer_23
  assign B = decoder_1_out23 ? register_24_q : 32'bz;  // Controlled_Buffer controlled_buffer_24
  assign B = decoder_1_out24 ? register_25_q : 32'bz;  // Controlled_Buffer controlled_buffer_25
  assign B = decoder_1_out25 ? register_26_q : 32'bz;  // Controlled_Buffer controlled_buffer_26
  assign B = decoder_1_out26 ? register_27_q : 32'bz;  // Controlled_Buffer controlled_buffer_27
  assign B = decoder_1_out27 ? register_28_q : 32'bz;  // Controlled_Buffer controlled_buffer_28
  assign B = decoder_1_out28 ? register_29_q : 32'bz;  // Controlled_Buffer controlled_buffer_29
  assign B = decoder_1_out29 ? register_30_q : 32'bz;  // Controlled_Buffer controlled_buffer_30
  assign B = decoder_1_out30 ? register_31_q : 32'bz;  // Controlled_Buffer controlled_buffer_31
  assign B = decoder_1_out31 ? register_32_q : 32'bz;  // Controlled_Buffer controlled_buffer_32
  assign A = decoder_2_out0 ? register_1_q : 32'bz;  // Controlled_Buffer controlled_buffer_33
  assign A = decoder_2_out1 ? register_2_q : 32'bz;  // Controlled_Buffer controlled_buffer_34
  assign A = decoder_2_out2 ? register_3_q : 32'bz;  // Controlled_Buffer controlled_buffer_35
  assign A = decoder_2_out3 ? register_4_q : 32'bz;  // Controlled_Buffer controlled_buffer_36
  assign A = decoder_2_out4 ? register_5_q : 32'bz;  // Controlled_Buffer controlled_buffer_37
  assign A = decoder_2_out5 ? register_6_q : 32'bz;  // Controlled_Buffer controlled_buffer_38
  assign A = decoder_2_out6 ? register_7_q : 32'bz;  // Controlled_Buffer controlled_buffer_39
  assign A = decoder_2_out7 ? register_8_q : 32'bz;  // Controlled_Buffer controlled_buffer_40
  assign A = decoder_2_out8 ? register_9_q : 32'bz;  // Controlled_Buffer controlled_buffer_41
  assign A = decoder_2_out9 ? register_10_q : 32'bz;  // Controlled_Buffer controlled_buffer_42
  assign A = decoder_2_out10 ? register_11_q : 32'bz;  // Controlled_Buffer controlled_buffer_43
  assign A = decoder_2_out11 ? register_12_q : 32'bz;  // Controlled_Buffer controlled_buffer_44
  assign A = decoder_2_out12 ? register_13_q : 32'bz;  // Controlled_Buffer controlled_buffer_45
  assign A = decoder_2_out13 ? register_14_q : 32'bz;  // Controlled_Buffer controlled_buffer_46
  assign A = decoder_2_out14 ? register_15_q : 32'bz;  // Controlled_Buffer controlled_buffer_47
  assign A = decoder_2_out15 ? register_16_q : 32'bz;  // Controlled_Buffer controlled_buffer_48
  assign A = decoder_2_out16 ? register_17_q : 32'bz;  // Controlled_Buffer controlled_buffer_49
  assign A = decoder_2_out17 ? register_18_q : 32'bz;  // Controlled_Buffer controlled_buffer_50
  assign A = decoder_2_out18 ? register_19_q : 32'bz;  // Controlled_Buffer controlled_buffer_51
  assign A = decoder_2_out19 ? register_20_q : 32'bz;  // Controlled_Buffer controlled_buffer_52
  assign A = decoder_2_out20 ? register_21_q : 32'bz;  // Controlled_Buffer controlled_buffer_53
  assign A = decoder_2_out21 ? register_22_q : 32'bz;  // Controlled_Buffer controlled_buffer_54
  assign A = decoder_2_out22 ? register_23_q : 32'bz;  // Controlled_Buffer controlled_buffer_55
  assign A = decoder_2_out23 ? register_24_q : 32'bz;  // Controlled_Buffer controlled_buffer_56
  assign A = decoder_2_out24 ? register_25_q : 32'bz;  // Controlled_Buffer controlled_buffer_57
  assign A = decoder_2_out25 ? register_26_q : 32'bz;  // Controlled_Buffer controlled_buffer_58
  assign A = decoder_2_out26 ? register_27_q : 32'bz;  // Controlled_Buffer controlled_buffer_59
  assign A = decoder_2_out27 ? register_28_q : 32'bz;  // Controlled_Buffer controlled_buffer_60
  assign A = decoder_2_out28 ? register_29_q : 32'bz;  // Controlled_Buffer controlled_buffer_61
  assign A = decoder_2_out29 ? register_30_q : 32'bz;  // Controlled_Buffer controlled_buffer_62
  assign A = decoder_2_out30 ? register_31_q : 32'bz;  // Controlled_Buffer controlled_buffer_63
  assign A = decoder_2_out31 ? register_32_q : 32'bz;  // Controlled_Buffer controlled_buffer_64
endmodule

module \ID_수업  (
  input  [31:0] ALU,
  input  [31:0] Mem,
  input  [31:0] Instruction,
  input  in_4,
  output Branch,
  output MemRead,
  output MemWrite,
  output [2:0] ALUop,
  output [31:0] A,
  output [31:0] B,
  output [31:0] D,
  output [31:0] Offset
);

  wire clock_1_out;
  wire [1:0] bit_extender_2_out;
  wire [2:0] rom_2_data;
  wire [4:0] multiplexer_2_out;
  wire [9:0] rom_1_data;
  wire [31:0] multiplexer_1_out, register_file_1_b, shifter_1_out, shifter_2_out, shifter_3_out;

  Multiplexer #(.width(32), .enable("false")) multiplexer_1 (
    .in0(ALU), .in1(Mem), .out(multiplexer_1_out), .sel(rom_1_data[6]));
  Multiplexer #(.width(5), .enable("false")) multiplexer_2 (
    .in0(Instruction[20:16]), .in1(Instruction[15:11]), .out(multiplexer_2_out), .sel(rom_1_data[9]));
  Clock clock_1 (.out(clock_1_out));
  assign Offset = {{16{Instruction[15]}}, Instruction[15:0]};  // Bit_Extender bit_extender_1
  ROM #(.addrWidth(6), .dataWidth(10)) rom_1 (
    .addr(Instruction[31:26]),
    .data({rom_1_data[9], Branch, MemRead, rom_1_data[6:3], MemWrite, rom_1_data[1:0]}));  // open: sel
  register_file register_file_1 (
    .C(multiplexer_1_out), .rd(multiplexer_2_out), .rs(Instruction[25:21]), .rt(Instruction[20:16]), .A(A),
    .B(register_file_1_b), .clk(clock_1_out), .load(rom_1_data[0]), .clear(in_4));
  Multiplexer #(.width(32), .enable("false")) multiplexer_3 (
    .in0(register_file_1_b), .in1(Offset), .out(B), .sel(rom_1_data[1]));
  Shifter #(.width(32)) shifter_1 (.in(register_file_1_b), .\dist (Instruction[10:6]), .out(shifter_1_out));
  Shifter #(.width(32), .shift("lr")) shifter_2 (
    .in(register_file_1_b), .\dist (Instruction[10:6]), .out(shifter_2_out));
  Shifter #(.width(32), .shift("ar")) shifter_3 (
    .in(register_file_1_b), .\dist (Instruction[10:6]), .out(shifter_3_out));
  Bit_Extender #(.in_width(6), .out_width(2), .\type ("sign")) bit_extender_2 (
    .in(Instruction[5:0]), .out(bit_extender_2_out));
  ROM #(.addrWidth(6), .dataWidth(3)) rom_2 (.addr(Instruction[5:0]), .data(rom_2_data));  // open: sel
  Multiplexer #(.width(3), .enable("false")) multiplexer_4 (
    .in0(rom_1_data[5:3]), .in1(rom_2_data), .out(ALUop), .sel(rom_1_data[9]));
  Multiplexer #(.select(2), .width(32), .enable("false")) multiplexer_5 (
    .in0(shifter_1_out), .in2(shifter_2_out), .in3(shifter_3_out), .out(D), .sel(bit_extender_2_out));  // open: in1

  // Notes on the sheet:
  //   MemToReg
  //   op
  //   shampt
  //   funct
  //   RegDst
  //   Control Unit (ROM Unit)
  //   contents of rom_1 (hex, n*v repeats v):
  //   234 0 0 0 140 140 0 0 3 0 0 0 3 3 3 20*0 c3 7*0 6 10*0 c3 7*0 6
  //   RegWrite
  //   ALUSrc
  //   ALU Control Unit
  //   for R-type instruction
  //   sll
  //   srl
  //   sra
endmodule

module ALU (
  input  [31:0] A,
  input  [31:0] B,
  input  [2:0] ALU_op,
  output [31:0] C,
  output zero
);

  wire [31:0] adder_1_out, AND_out, divider_1_out, multiplier_1_out, NOR_out, OR_out, subtractor_1_out,
       XOR_out;

  Adder #(.width(32)) adder_1 (.a(A), .b(B), .out(adder_1_out));  // open: cin, cout
  Subtractor #(.width(32)) subtractor_1 (.a(A), .b(B), .out(subtractor_1_out));  // open: bin, bout
  Multiplier #(.width(32)) multiplier_1 (.a(A), .b(B), .out(multiplier_1_out));  // open: cin, cout
  Divider #(.width(32)) divider_1 (.a(A), .b(B), .out(divider_1_out));  // open: upper, rem
  assign AND_out = A & B;  // AND_Gate AND, 32 bits wide
  assign OR_out = A | B;  // OR_Gate OR, 32 bits wide
  assign XOR_out = A ^ B;  // XOR_Gate XOR, 32 bits wide
  assign NOR_out = ~(A | B);  // NOR_Gate NOR, 32 bits wide
  Comparator #(.width(32)) comparator_1 (.a(B), .b(A), .eq(zero));  // open: gt, lt
  Multiplexer #(.select(3), .width(32), .enable("false")) multiplexer_1 (
    .in0(adder_1_out), .in1(subtractor_1_out), .in2(multiplier_1_out), .in3(divider_1_out), .in4(AND_out),
    .in5(OR_out), .in6(XOR_out), .in7(NOR_out), .out(C), .sel(ALU_op));
endmodule

module \Memory_수업  (
  input  [31:0] address,
  input  [31:0] D_in,
  input  Write,
  input  Read,
  output [31:0] D_out
);

  wire clock_1_out;

  Clock clock_1 (.out(clock_1_out));
  RAM #(.dataWidth(32), .bus("separate")) ram_1 (
    .addr(address[9:2]), .din(D_in), .data(D_out), .str(Write), .clk(clock_1_out), .ld(Read));  // open: sel, clr
endmodule

module \MIPS_수업  (
  input  clear
);

  wire alu_1_zero, \id_수업_1_branch , \id_수업_1_memread , \id_수업_1_memwrite ;
  wire [2:0] \id_수업_1_aluop ;
  wire [31:0] alu_1_c, \id_수업_1_a , \id_수업_1_b , \id_수업_1_d , \id_수업_1_offset , \if_수업_1_out_5 ,
       \memory_수업_1_d_out ;

  \IF_수업  \if_수업_1  (
    .clear(clear), .out_5(\if_수업_1_out_5 ), .branch(\id_수업_1_branch ), .offset(\id_수업_1_offset ),
    .Zero(alu_1_zero));
  \ID_수업  \id_수업_1  (
    .Instruction(\if_수업_1_out_5 ), .ALU(alu_1_c), .A(\id_수업_1_a ), .B(\id_수업_1_b ),
    .Offset(\id_수업_1_offset ), .MemWrite(\id_수업_1_memwrite ), .Branch(\id_수업_1_branch ),
    .Mem(\memory_수업_1_d_out ), .ALUop(\id_수업_1_aluop ), .in_4(clear), .MemRead(\id_수업_1_memread ),
    .D(\id_수업_1_d ));
  ALU alu_1 (.A(\id_수업_1_a ), .B(\id_수업_1_b ), .ALU_op(\id_수업_1_aluop ), .C(alu_1_c), .zero(alu_1_zero));
  \Memory_수업  \memory_수업_1  (
    .address(alu_1_c), .D_in(\id_수업_1_d ), .Write(\id_수업_1_memwrite ), .D_out(\memory_수업_1_d_out ),
    .Read(\id_수업_1_memread ));
endmodule
